# Fritzing sketch cablage_arduino_fritzing (saved by Fritzing 0.9.4)
breadboards: 1

parts:
  Composant1 = Arduino Mega 2560 (Rev3)
  Adafruit_HUZZAH_ESP8266_Breakout1 = Adafruit HUZZAH ESP8266 Breakout [part_number=2471]  # not connected
  Grove1 = Grove OLED 128x96
  P1 = S1133 Si Photodiode [package="8mm Ceramic [THT]"]
  S2 = Pushbutton [package="[THT]"]
  LED1 = RGB LED (com. anode, rbg) [package="5 mm [THT]"]  # not connected
  LED2 = RGB LED (com. anode, rbg) [package="5 mm [THT]"]  # not connected
  LED3 = RGB LED (com. anode, rbg) [package="5 mm [THT]"]  # not connected
  LED4 = RGB LED (com. anode, rbg) [package="5 mm [THT]"]  # not connected
  LED5 = RGB LED (com. anode, rbg) [package="5 mm [THT]"]  # not connected
  U1 = POT [package=pot_alpha_rv16af-20]  # not connected
  R1 = Resistor [tolerance=±5% resistance=220 package="0805 [SMD]"]
  IR1 = TSOP312.., 314.. [package=THT]  # not connected
  RHT1 = Humidity and Temperature Sensor RHT03
  R2 = Resistor [tolerance=±5% resistance=220 package=THT]

nets:
  VCC: Composant1.5V, Grove1.VCC, RHT1.Vcc, R2.Pin_0
  GND: Composant1.GND, Composant1.D4_PWM, Grove1.GND, P1.anode, S2.Pin_3, S2.Pin_4, RHT1.GND_2
  N1: Composant1.D2_PWM, R1.Pin_0
  N2: Composant1.D3_PWM, RHT1.GND_1
  N3: P1.cathode, R1.Pin_1
  N4: S2.Pin_1, S2.Pin_2
  N5: RHT1.Data-signal, R2.Pin_1
